// Logisim project refactor.circ as structural Verilog: 20 circuits, main circuit main
module main (
  input  enable,
  output [11:0] PC
);

  wire and_1_out, button_1_out, clear_out, clk_out, execute_1_cnd, or_1_out, pcupdate_1_halt;
  wire [3:0] fetch_1_icode, fetch_1_ifun, fetch_1_ra, fetch_1_rb;
  wire [11:0] fetch_1_valp;
  wire [63:0] decode_1_vala, decode_1_valb, execute_1_vale, fetch_1_valc, memory_1_valm;

  Button clear (.out(clear_out));
  Button button_1 (.out(button_1_out));
  Clock clk (.out(clk_out));
  or or_1 (or_1_out, button_1_out, clk_out);
  and and_1 (and_1_out, enable, ~pcupdate_1_halt);  // AND_Gate
  fetch fetch_1 (
    .PC(PC), .clk(or_1_out), .e(and_1_out), .c(clear_out), .icode(fetch_1_icode), .ifun(fetch_1_ifun),
    .rA(fetch_1_ra), .rB(fetch_1_rb), .valC(fetch_1_valc), .valP(fetch_1_valp));
  decode decode_1 (
    .WB_valM(memory_1_valm), .icode(fetch_1_icode), .rA(fetch_1_ra), .rB(fetch_1_rb), .c(clear_out),
    .e(and_1_out), .clk(or_1_out), .WB_valE(execute_1_vale), .valA(decode_1_vala), .valB(decode_1_valb));
  execute execute_1 (
    .icode(fetch_1_icode), .ifun(fetch_1_ifun), .valA(decode_1_vala), .valB(decode_1_valb),
    .valC(fetch_1_valc), .clock(or_1_out), .c(clear_out), .e(and_1_out), .ValE(execute_1_vale),
    .Cnd(execute_1_cnd));
  memory memory_1 (
    .iCode(fetch_1_icode), .valA(decode_1_vala), .valE(execute_1_vale), .valP(fetch_1_valp), .e(and_1_out),
    .c(clear_out), .clk(or_1_out), .valM(memory_1_valm));
  pcUpdate pcupdate_1 (
    .iCode(fetch_1_icode), .valP(fetch_1_valp), .valC(fetch_1_valc), .valM(memory_1_valm),
    .Cnd(execute_1_cnd), .clk(or_1_out), .c(clear_out), .e(and_1_out), .halt(pcupdate_1_halt), .PC(PC));
endmodule

module instructionMem (
  input  [11:0] PC,
  input  clk,
  input  e,
  input  c,
  output [7:0] b0,
  output [7:0] b1,
  output [7:0] b2,
  output [7:0] b3,
  output [7:0] b4,
  output [7:0] b5,
  output [7:0] b6,
  output [7:0] b7,
  output [7:0] b8,
  output [7:0] b9
);

  wire and_1_out, comparator_1_eq, decoder_1_out0, decoder_1_out1, decoder_1_out2, decoder_1_out3,
       decoder_1_out4, decoder_1_out5, decoder_1_out6, decoder_1_out7, decoder_1_out8, decoder_1_out9,
       or_1_out;
  wire [7:0] multiplexer_1_out, multiplexer_2_out, multiplexer_3_out, multiplexer_4_out, multiplexer_5_out,
       multiplexer_6_out, multiplexer_7_out, multiplexer_8_out, multiplexer_9_out, multiplexer_10_out,
       rom_1_data;
  wire [11:0] adder_1_out, counter_1_q;

  or or_1 (or_1_out, c, comparator_1_eq);
  Counter #(.max('hfff), .width(12)) counter_1 (
    .clr(or_1_out), .up(1'b1), .clk(and_1_out), .Q(counter_1_q));  // open: load, count, D, carry
  and and_1 (and_1_out, e, clk);
  // AND_Gate and_2 is placed but not wired
  // AND_Gate and_3 is placed but not wired
  // AND_Gate and_4 is placed but not wired
  // AND_Gate and_5 is placed but not wired
  ROM #(.addrWidth(12)) rom_1 (.addr(adder_1_out), .data(rom_1_data));
  Adder #(.width(12)) adder_1 (.a(PC), .b(counter_1_q), .out(adder_1_out));  // open: cin, cout
  Comparator #(.width(12)) comparator_1 (.a(counter_1_q), .b(12'h14), .eq(comparator_1_eq));  // open: gt, lt
  Decoder #(.select(5)) decoder_1 (
    .out0(decoder_1_out0), .out1(decoder_1_out1), .out2(decoder_1_out2), .out3(decoder_1_out3),
    .out4(decoder_1_out4), .out5(decoder_1_out5), .out6(decoder_1_out6), .out7(decoder_1_out7),
    .out8(decoder_1_out8), .out9(decoder_1_out9), .sel(counter_1_q[4:0]), .en(1'b1));  // open: out10, out11, out12, out13, out14, out15, out16, out17, out18, out19, out20, out21, out22, out23, out24, out25, out26, out27, out28, out29, out30, out31
  Register register_1 (.D(multiplexer_1_out), .en(e), .clk(clk), .Q(b0));  // open: clr
  Multiplexer #(.width(8)) multiplexer_1 (.in0(b0), .in1(rom_1_data), .out(multiplexer_1_out), .sel(decoder_1_out0));
  Register register_2 (.D(multiplexer_2_out), .en(e), .clk(clk), .Q(b1));  // open: clr
  Multiplexer #(.width(8)) multiplexer_2 (.in0(b1), .in1(rom_1_data), .out(multiplexer_2_out), .sel(decoder_1_out1));
  Register register_3 (.D(multiplexer_3_out), .en(e), .clk(clk), .Q(b2));  // open: clr
  Multiplexer #(.width(8)) multiplexer_3 (.in0(b2), .in1(rom_1_data), .out(multiplexer_3_out), .sel(decoder_1_out2));
  Register register_4 (.D(multiplexer_4_out), .en(e), .clk(clk), .Q(b3));  // open: clr
  Multiplexer #(.width(8)) multiplexer_4 (.in0(b3), .in1(rom_1_data), .out(multiplexer_4_out), .sel(decoder_1_out3));
  Register register_5 (.D(multiplexer_5_out), .en(e), .clk(clk), .Q(b4));  // open: clr
  Multiplexer #(.width(8)) multiplexer_5 (.in0(b4), .in1(rom_1_data), .out(multiplexer_5_out), .sel(decoder_1_out4));
  Register register_6 (.D(multiplexer_6_out), .en(e), .clk(clk), .Q(b5));  // open: clr
  Multiplexer #(.width(8)) multiplexer_6 (.in0(b5), .in1(rom_1_data), .out(multiplexer_6_out), .sel(decoder_1_out5));
  Register register_7 (.D(multiplexer_7_out), .en(e), .clk(clk), .Q(b6));  // open: clr
  Multiplexer #(.width(8)) multiplexer_7 (.in0(b6), .in1(rom_1_data), .out(multiplexer_7_out), .sel(decoder_1_out6));
  Register register_8 (.D(multiplexer_8_out), .en(e), .clk(clk), .Q(b7));  // open: clr
  Multiplexer #(.width(8)) multiplexer_8 (.in0(b7), .in1(rom_1_data), .out(multiplexer_8_out), .sel(decoder_1_out7));
  Register register_9 (.D(multiplexer_9_out), .en(e), .clk(clk), .Q(b8));  // open: clr
  Multiplexer #(.width(8)) multiplexer_9 (.in0(b8), .in1(rom_1_data), .out(multiplexer_9_out), .sel(decoder_1_out8));
  Register register_10 (.D(multiplexer_10_out), .en(e), .clk(clk), .Q(b9));  // open: clr
  Multiplexer #(.width(8)) multiplexer_10 (.in0(b9), .in1(rom_1_data), .out(multiplexer_10_out), .sel(decoder_1_out9));

  // Notes on the sheet:
  //   contents of rom_1 (hex, n*v repeats v):
  //   30 f4 6*0 2 0 80 7*0 14 0 30 f1 7*0 5 30 f2 6*0 3 0 30 f3 7*0 7 40 32 8*0 30 f3 7*0 5 40 32 7*0 8 30
  //   f3 7*0 6 40 32 7*0 10 30 f3 7*0 8 40 32 7*0 18 30 f3 7*0 1 40 32 7*0 20 a0 2f a0 1f 10 10 10 80 7*0
  //   a1 b0 8f b0 8f 90 50 84 7*0 8 50 94 7*0 10 50 a4 7*0 8 30 fb 8*0 30 fc 7*0 1 30 f1 7*0 8 61 ba 73
  //   6*0 1 51 61 ca 50 d4 7*0 8 50 e4 7*0 10 60 1e 61 cd 73 7*0 dd 61 1e 50 6e 8*0 50 7e 7*0 8 60 1e 61
  //   67 75 7*0 fe 60 67 40 6e 8*0 61 1e 40 7e 8*0 60 1e 70 7*0 fe 90
endmodule

module fetch (
  input  [11:0] PC,
  input  clk,
  input  e,
  input  c,
  output [3:0] icode,
  output [3:0] ifun,
  output [3:0] rA,
  output [3:0] rB,
  output [63:0] valC,
  output [11:0] valP
);

  wire needsreg_1_needreg, needsvalc_1_needvalc;
  wire [7:0] instructionmem_1_b1, instructionmem_1_b2, instructionmem_1_b3, instructionmem_1_b4,
       instructionmem_1_b5, instructionmem_1_b6, instructionmem_1_b7, instructionmem_1_b8,
       instructionmem_1_b9;

  instructionMem instructionmem_1 (
    .PC(PC), .clk(clk), .e(e), .c(c), .b0({icode, ifun}), .b1(instructionmem_1_b1), .b2(instructionmem_1_b2),
    .b3(instructionmem_1_b3), .b4(instructionmem_1_b4), .b5(instructionmem_1_b5), .b6(instructionmem_1_b6),
    .b7(instructionmem_1_b7), .b8(instructionmem_1_b8), .b9(instructionmem_1_b9));
  needsReg needsreg_1 (.icode(icode), .needReg(needsreg_1_needreg));
  align align_1 (
    .needReg(needsreg_1_needreg), .b1(instructionmem_1_b1), .b2(instructionmem_1_b2),
    .b3(instructionmem_1_b3), .b4(instructionmem_1_b4), .b5(instructionmem_1_b5), .b6(instructionmem_1_b6),
    .b7(instructionmem_1_b7), .b8(instructionmem_1_b8), .b9(instructionmem_1_b9), .rA(rA), .rB(rB),
    .valC(valC));
  needsValC needsvalc_1 (.icode(icode), .needValC(needsvalc_1_needvalc));
  pcInc pcinc_1 (.PC(PC), .needsReg(needsreg_1_needreg), .needsValC(needsvalc_1_needvalc), .valP(valP));
endmodule

module align (
  input  needReg,
  input  [7:0] b1,
  input  [7:0] b2,
  input  [7:0] b3,
  input  [7:0] b4,
  input  [7:0] b5,
  input  [7:0] b6,
  input  [7:0] b7,
  input  [7:0] b8,
  input  [7:0] b9,
  output [3:0] rA,
  output [3:0] rB,
  output [63:0] valC
);

  Multiplexer #(.width(64)) multiplexer_1 (
    .in0({b1, b2, b3, b4, b5, b6, b7, b8}), .in1({b2, b3, b4, b5, b6, b7, b8, b9}), .out(valC), .sel(needReg));

  assign rA = b1[7:4];
  assign rB = b1[3:0];
endmodule

module needsReg (
  input  [3:0] icode,
  output needReg
);

  wire and_1_out, and_2_out, and_3_out, and_4_out, and_5_out, and_6_out, and_7_out;

  and and_1 (and_1_out, ~icode[0], icode[1], ~icode[2], ~icode[3]);  // AND_Gate
  and and_2 (and_2_out, icode[0], icode[1], ~icode[2], ~icode[3]);  // AND_Gate
  and and_3 (and_3_out, ~icode[0], ~icode[1], icode[2], ~icode[3]);  // AND_Gate
  and and_4 (and_4_out, icode[0], ~icode[1], icode[2], ~icode[3]);  // AND_Gate
  and and_5 (and_5_out, ~icode[0], icode[1], icode[2], ~icode[3]);  // AND_Gate
  and and_6 (and_6_out, ~icode[0], icode[1], ~icode[2], icode[3]);  // AND_Gate
  and and_7 (and_7_out, icode[0], icode[1], ~icode[2], icode[3]);  // AND_Gate
  or or_1 (needReg, and_1_out, and_2_out, and_3_out, and_4_out, and_5_out, and_6_out, and_7_out);
endmodule

module needsValC (
  input  [3:0] icode,
  output needValC
);

  wire and_1_out, and_2_out, and_3_out, and_4_out, and_5_out;

  and and_1 (and_1_out, icode[0], icode[1], ~icode[2], ~icode[3]);  // AND_Gate
  and and_2 (and_2_out, ~icode[0], ~icode[1], icode[2], ~icode[3]);  // AND_Gate
  and and_3 (and_3_out, icode[0], ~icode[1], icode[2], ~icode[3]);  // AND_Gate
  and and_4 (and_4_out, icode[0], icode[1], icode[2], ~icode[3]);  // AND_Gate
  and and_5 (and_5_out, ~icode[0], ~icode[1], ~icode[2], icode[3]);  // AND_Gate
  or or_1 (needValC, and_1_out, and_2_out, and_3_out, and_4_out, and_5_out);
endmodule

module pcInc (
  input  [11:0] PC,
  input  needsReg,
  input  needsValC,
  output [11:0] valP
);

  wire [11:0] adder_1_out, adder_2_out, multiplexer_1_out, multiplexer_2_out;

  Multiplexer #(.width(12)) multiplexer_1 (.in0({12{1'b0}}), .in1(12'h1), .out(multiplexer_1_out), .sel(needsReg));
  Multiplexer #(.width(12)) multiplexer_2 (.in0({12{1'b0}}), .in1(12'h8), .out(multiplexer_2_out), .sel(needsValC));
  Adder #(.width(12)) adder_1 (.a(multiplexer_1_out), .b(multiplexer_2_out), .out(adder_1_out));  // open: cin, cout
  Adder #(.width(12)) adder_2 (.a(12'h1), .b(adder_1_out), .out(adder_2_out));  // open: cin, cout
  Adder #(.width(12)) adder_3 (.a(PC), .b(adder_2_out), .out(valP));  // open: cin, cout
endmodule

module regFile (
  input  [63:0] W_dataM,
  input  [3:0] W_addrM,
  input  [3:0] R_addrA,
  input  [63:0] WdataE,
  input  [3:0] W_addrE,
  input  [3:0] R_addrB,
  input  c,
  input  e,
  input  clk,
  output [63:0] valA,
  output [63:0] valB
);

  wire and_1_out, and_2_out, comparator_1_eq, comparator_2_eq, or_1_out, or_2_out, or_3_out, or_4_out,
       or_5_out, or_6_out, or_7_out, or_8_out, or_9_out, or_10_out, or_11_out, or_12_out, or_13_out,
       or_14_out, or_15_out, or_16_out, or_17_out;
  wire [1:0] decoder_2_out0, decoder_2_out1, decoder_2_out2, decoder_2_out3, decoder_2_out4, decoder_2_out5,
       decoder_2_out6, decoder_2_out7, decoder_2_out8, decoder_2_out9, decoder_2_out10, decoder_2_out11,
       decoder_2_out12, decoder_2_out13, decoder_2_out14, decoder_2_out15;
  wire [7:0] counter_1_q;
  wire [63:0] multiplexer_1_out, multiplexer_2_out, multiplexer_3_out, multiplexer_4_out, multiplexer_5_out,
       multiplexer_6_out, multiplexer_7_out, multiplexer_8_out, multiplexer_9_out, multiplexer_10_out,
       multiplexer_11_out, multiplexer_12_out, multiplexer_13_out, multiplexer_14_out, multiplexer_15_out,
       multiplexer_16_out, register_1_q, register_2_q, register_3_q, register_4_q, register_5_q,
       register_6_q, register_7_q, register_8_q, register_9_q, register_10_q, register_11_q, register_12_q,
       register_13_q, register_14_q, register_15_q, register_16_q;

  Decoder #(.select(4)) decoder_1 (
    .out0(decoder_2_out0[1]), .out1(decoder_2_out1[1]), .out2(decoder_2_out2[1]), .out3(decoder_2_out3[1]),
    .out4(decoder_2_out4[1]), .out5(decoder_2_out5[1]), .out6(decoder_2_out6[1]), .out7(decoder_2_out7[1]),
    .out8(decoder_2_out8[1]), .out9(decoder_2_out9[1]), .out10(decoder_2_out10[1]),
    .out11(decoder_2_out11[1]), .out12(decoder_2_out12[1]), .out13(decoder_2_out13[1]),
    .out14(decoder_2_out14[1]), .out15(decoder_2_out15[1]), .sel(W_addrE));  // open: en
  and and_1 (and_1_out, clk, e);
  Decoder #(.select(4)) decoder_2 (
    .out0(decoder_2_out0[0]), .out1(decoder_2_out1[0]), .out2(decoder_2_out2[0]), .out3(decoder_2_out3[0]),
    .out4(decoder_2_out4[0]), .out5(decoder_2_out5[0]), .out6(decoder_2_out6[0]), .out7(decoder_2_out7[0]),
    .out8(decoder_2_out8[0]), .out9(decoder_2_out9[0]), .out10(decoder_2_out10[0]),
    .out11(decoder_2_out11[0]), .out12(decoder_2_out12[0]), .out13(decoder_2_out13[0]),
    .out14(decoder_2_out14[0]), .out15(decoder_2_out15[0]), .sel(W_addrM));  // open: en
  Counter counter_1 (.clr(or_1_out), .count(1'b1), .clk(and_1_out), .Q(counter_1_q));  // open: load, up, D, carry
  or or_1 (or_1_out, c, comparator_2_eq);
  Multiplexer #(.select(2), .width(64)) multiplexer_1 (
    .in1(W_dataM), .in2(WdataE), .out(multiplexer_1_out), .sel(decoder_2_out0));  // open: in0, in3
  Multiplexer #(.select(2), .width(64)) multiplexer_2 (
    .in1(W_dataM), .in2(WdataE), .out(multiplexer_2_out), .sel(decoder_2_out1));  // open: in0, in3
  Multiplexer #(.select(2), .width(64)) multiplexer_3 (
    .in1(W_dataM), .in2(WdataE), .out(multiplexer_3_out), .sel(decoder_2_out2));  // open: in0, in3
  Multiplexer #(.select(2), .width(64)) multiplexer_4 (
    .in1(W_dataM), .in2(WdataE), .out(multiplexer_4_out), .sel(decoder_2_out3));  // open: in0, in3
  Multiplexer #(.select(2), .width(64)) multiplexer_5 (
    .in1(W_dataM), .in2(WdataE), .out(multiplexer_5_out), .sel(decoder_2_out4));  // open: in0, in3
  Multiplexer #(.select(2), .width(64)) multiplexer_6 (
    .in1(W_dataM), .in2(WdataE), .out(multiplexer_6_out), .sel(decoder_2_out5));  // open: in0, in3
  Multiplexer #(.select(2), .width(64)) multiplexer_7 (
    .in1(W_dataM), .in2(WdataE), .out(multiplexer_7_out), .sel(decoder_2_out6));  // open: in0, in3
  Multiplexer #(.select(2), .width(64)) multiplexer_8 (
    .in1(W_dataM), .in2(WdataE), .out(multiplexer_8_out), .sel(decoder_2_out7));  // open: in0, in3
  Multiplexer #(.select(2), .width(64)) multiplexer_9 (
    .in1(W_dataM), .in2(WdataE), .out(multiplexer_9_out), .sel(decoder_2_out8));  // open: in0, in3
  Multiplexer #(.select(2), .width(64)) multiplexer_10 (
    .in1(W_dataM), .in2(WdataE), .out(multiplexer_10_out), .sel(decoder_2_out9));  // open: in0, in3
  Multiplexer #(.select(2), .width(64)) multiplexer_11 (
    .in1(W_dataM), .in2(WdataE), .out(multiplexer_11_out), .sel(decoder_2_out10));  // open: in0, in3
  Multiplexer #(.select(2), .width(64)) multiplexer_12 (
    .in1(W_dataM), .in2(WdataE), .out(multiplexer_12_out), .sel(decoder_2_out11));  // open: in0, in3
  Multiplexer #(.select(2), .width(64)) multiplexer_13 (
    .in1(W_dataM), .in2(WdataE), .out(multiplexer_13_out), .sel(decoder_2_out12));  // open: in0, in3
  Multiplexer #(.select(2), .width(64)) multiplexer_14 (
    .in1(W_dataM), .in2(WdataE), .out(multiplexer_14_out), .sel(decoder_2_out13));  // open: in0, in3
  Multiplexer #(.select(2), .width(64)) multiplexer_15 (
    .in1(W_dataM), .in2(WdataE), .out(multiplexer_15_out), .sel(decoder_2_out14));  // open: in0, in3
  Multiplexer #(.select(2), .width(64)) multiplexer_16 (
    .in1(W_dataM), .in2(WdataE), .out(multiplexer_16_out), .sel(decoder_2_out15));  // open: in0, in3
  Comparator comparator_1 (.a({8{1'b0}}), .b(counter_1_q), .eq(comparator_1_eq));  // open: gt, lt
  or or_2 (or_2_out, decoder_2_out0[0], decoder_2_out0[1]);
  or or_3 (or_3_out, decoder_2_out1[0], decoder_2_out1[1]);
  or or_4 (or_4_out, decoder_2_out2[0], decoder_2_out2[1]);
  or or_5 (or_5_out, decoder_2_out3[0], decoder_2_out3[1]);
  or or_6 (or_6_out, decoder_2_out4[0], decoder_2_out4[1]);
  or or_7 (or_7_out, decoder_2_out5[0], decoder_2_out5[1]);
  or or_8 (or_8_out, decoder_2_out6[0], decoder_2_out6[1]);
  or or_9 (or_9_out, decoder_2_out7[0], decoder_2_out7[1]);
  or or_10 (or_10_out, decoder_2_out8[0], decoder_2_out8[1]);
  or or_11 (or_11_out, decoder_2_out9[0], decoder_2_out9[1]);
  or or_12 (or_12_out, decoder_2_out10[0], decoder_2_out10[1]);
  or or_13 (or_13_out, decoder_2_out11[0], decoder_2_out11[1]);
  or or_14 (or_14_out, decoder_2_out12[0], decoder_2_out12[1]);
  or or_15 (or_15_out, decoder_2_out13[1], decoder_2_out13[0]);
  or or_16 (or_16_out, decoder_2_out14[0], decoder_2_out14[1]);
  or or_17 (or_17_out, decoder_2_out15[0], decoder_2_out15[1]);
  and and_2 (and_2_out, ~clk, comparator_1_eq);  // AND_Gate
  Comparator comparator_2 (.a(8'h14), .b(counter_1_q), .eq(comparator_2_eq));  // open: gt, lt
  Register #(.width(64)) register_1 (
    .D(multiplexer_1_out), .en(or_2_out), .clk(and_2_out), .Q(register_1_q));  // open: clr
  Register #(.width(64)) register_2 (
    .D(multiplexer_2_out), .en(or_3_out), .clk(and_2_out), .Q(register_2_q));  // open: clr
  Register #(.width(64)) register_3 (
    .D(multiplexer_3_out), .en(or_4_out), .clk(and_2_out), .Q(register_3_q));  // open: clr
  Register #(.width(64)) register_4 (
    .D(multiplexer_4_out), .en(or_5_out), .clk(and_2_out), .Q(register_4_q));  // open: clr
  Register #(.width(64)) register_5 (
    .D(multiplexer_5_out), .en(or_6_out), .clk(and_2_out), .Q(register_5_q));  // open: clr
  Register #(.width(64)) register_6 (
    .D(multiplexer_6_out), .en(or_7_out), .clk(and_2_out), .Q(register_6_q));  // open: clr
  Register #(.width(64)) register_7 (
    .D(multiplexer_7_out), .en(or_8_out), .clk(and_2_out), .Q(register_7_q));  // open: clr
  Register #(.width(64)) register_8 (
    .D(multiplexer_8_out), .en(or_9_out), .clk(and_2_out), .Q(register_8_q));  // open: clr
  Register #(.width(64)) register_9 (
    .D(multiplexer_9_out), .en(or_10_out), .clk(and_2_out), .Q(register_9_q));  // open: clr
  Register #(.width(64)) register_10 (
    .D(multiplexer_10_out), .en(or_11_out), .clk(and_2_out), .Q(register_10_q));  // open: clr
  Register #(.width(64)) register_11 (
    .D(multiplexer_11_out), .en(or_12_out), .clk(and_2_out), .Q(register_11_q));  // open: clr
  Register #(.width(64)) register_12 (
    .D(multiplexer_12_out), .en(or_13_out), .clk(and_2_out), .Q(register_12_q));  // open: clr
  Register #(.width(64)) register_13 (
    .D(multiplexer_13_out), .en(or_14_out), .clk(and_2_out), .Q(register_13_q));  // open: clr
  Register #(.width(64)) register_14 (
    .D(multiplexer_14_out), .en(or_15_out), .clk(and_2_out), .Q(register_14_q));  // open: clr
  Register #(.width(64)) register_15 (
    .D(multiplexer_15_out), .en(or_16_out), .clk(and_2_out), .Q(register_15_q));  // open: clr
  Register #(.width(64)) register_16 (
    .D(multiplexer_16_out), .en(or_17_out), .clk(and_2_out), .Q(register_16_q));  // open: clr
  Multiplexer #(.select(4), .width(64)) multiplexer_17 (
    .in0(register_1_q), .in1(register_2_q), .in2(register_3_q), .in3(register_4_q), .in4(register_5_q),
    .in5(register_6_q), .in6(register_7_q), .in7(register_8_q), .in8(register_9_q), .in9(register_10_q),
    .in10(register_11_q), .in11(register_12_q), .in12(register_13_q), .in13(register_14_q),
    .in14(register_15_q), .in15(register_16_q), .out(valB), .sel(R_addrB));
  Multiplexer #(.select(4), .width(64)) multiplexer_18 (
    .in0(register_1_q), .in1(register_2_q), .in2(register_3_q), .in3(register_4_q), .in4(register_5_q),
    .in5(register_6_q), .in6(register_7_q), .in7(register_8_q), .in8(register_9_q), .in9(register_10_q),
    .in10(register_11_q), .in11(register_12_q), .in12(register_13_q), .in13(register_14_q),
    .in14(register_15_q), .in15(register_16_q), .out(valA), .sel(R_addrA));
endmodule

module ALU (
  input  [63:0] val1,
  input  [63:0] val2,
  input  [1:0] op,
  output [63:0] valE,
  output Negative,
  output Zero,
  output Overflow
);

  wire adder_1_cout, multiplexer_2_out, subtractor_1_bout;
  wire [63:0] adder_1_out, and_1_out, subtractor_1_out, xor_1_out;

  Adder #(.width(64)) adder_1 (.a(val1), .b(val2), .out(adder_1_out), .cout(adder_1_cout));  // open: cin
  Subtractor #(.width(64)) subtractor_1 (
    .a(val2), .b(val1), .out(subtractor_1_out), .bout(subtractor_1_bout));  // open: bin
  assign and_1_out = val2 & val1;  // AND_Gate and_1, 64 bits wide
  assign xor_1_out = val1 ^ val2;  // XOR_Gate xor_1, 64 bits wide
  Multiplexer #(.select(2), .width(64)) multiplexer_1 (
    .in0(adder_1_out), .in1(subtractor_1_out), .in2(and_1_out), .in3(xor_1_out),
    .out({Negative, valE[62:0]}), .sel(op));
  Multiplexer #(.select(2)) multiplexer_2 (
    .in0(adder_1_cout), .in1(subtractor_1_bout), .in2(1'b0), .in3(1'b0), .out(multiplexer_2_out), .sel(op));
  nor nor_1 (Zero, Negative, valE[62], valE[61], valE[60], valE[59], valE[58], valE[57], valE[56], valE[55], valE[54], valE[53], valE[52], valE[51], valE[50], valE[49], valE[48], valE[47], valE[46], valE[45], valE[44], valE[43], valE[42], valE[41], valE[40], valE[39], valE[38], valE[37], valE[36], valE[35], valE[34], valE[33], valE[32], valE[30], valE[29], valE[28], valE[27], valE[26], valE[25], valE[24], valE[23], valE[22], valE[21], valE[20], valE[19], valE[18], valE[17], valE[16], valE[15], valE[14], valE[13], valE[12], valE[11], valE[10], valE[9], valE[8], valE[7], valE[6], valE[5], valE[4], valE[3], valE[2], valE[1], valE[0], valE[31]);

  assign Overflow = 1'b0;
  assign valE[63] = Negative;
endmodule

module ALUB (
  input  [63:0] valB,
  input  [3:0] icode,
  output [63:0] val2
);

  wire and_1_out, and_2_out, or_1_out;

  and and_1 (and_1_out, ~icode[0], icode[1], ~icode[2], ~icode[3]);  // AND_Gate
  or or_1 (or_1_out, and_1_out, and_2_out);
  Multiplexer #(.width(64)) multiplexer_1 (.in0(valB), .in1({64{1'b0}}), .out(val2), .sel(or_1_out));
  and and_2 (and_2_out, icode[0], icode[1], ~icode[2], ~icode[3]);  // AND_Gate
endmodule

module ALUA (
  input  [63:0] valC,
  input  [63:0] valA,
  input  [3:0] icode,
  output [63:0] val1
);

  wire and_1_out, and_2_out, and_3_out, and_4_out, and_5_out;
  wire [1:0] or_1_out;

  and and_1 (and_1_out, ~icode[0], ~icode[1], icode[2], ~icode[3]);  // AND_Gate
  or or_1 (or_1_out[0], and_1_out, and_3_out, and_2_out);
  and and_2 (and_2_out, icode[0], ~icode[1], icode[2], ~icode[3]);  // AND_Gate
  and and_3 (and_3_out, icode[0], icode[1], ~icode[2], ~icode[3]);  // AND_Gate
  Multiplexer #(.select(2), .width(64)) multiplexer_1 (
    .in0(64'h8), .in1(valC), .in2(valA), .out(val1), .sel(or_1_out));  // open: in3
  or or_2 (or_1_out[1], and_4_out, and_5_out);
  and and_4 (and_4_out, ~icode[0], icode[1], ~icode[2], ~icode[3]);  // AND_Gate
  and and_5 (and_5_out, ~icode[0], icode[1], icode[2], ~icode[3]);  // AND_Gate
endmodule

module ALUfun (
  input  [3:0] icode,
  input  [3:0] ifun,
  output [1:0] op
);

  wire and_1_out, and_2_out, and_3_out, and_4_out, and_5_out, nor_1_out, or_1_out;

  nor nor_1 (nor_1_out, or_1_out, and_5_out, and_4_out);
  and and_1 (and_1_out, ~icode[0], icode[1], icode[2], ~icode[3], ifun[0], ~ifun[1], ~ifun[2], ~ifun[3]);  // AND_Gate
  or or_1 (or_1_out, and_1_out, and_2_out, and_3_out);
  and and_2 (and_2_out, ~icode[0], ~icode[1], ~icode[2], icode[3]);  // AND_Gate
  and and_3 (and_3_out, ~icode[0], icode[1], ~icode[2], icode[3]);  // AND_Gate
  Priority_Encoder #(.select(2)) priority_encoder_1 (
    .in0(nor_1_out), .in1(or_1_out), .in2(and_4_out), .in3(and_5_out), .out(op));
  and and_4 (and_4_out, ~icode[0], icode[1], icode[2], ~icode[3], ~ifun[0], ifun[1], ~ifun[2], ~ifun[3]);  // AND_Gate
  and and_5 (and_5_out, ~icode[0], icode[1], icode[2], ~icode[3], ifun[0], ifun[1], ~ifun[2], ~ifun[3]);  // AND_Gate
endmodule

module execute (
  input  [3:0] icode,
  input  [3:0] ifun,
  input  [63:0] valA,
  input  [63:0] valB,
  input  [63:0] valC,
  input  clock,
  input  c,
  input  e,
  output [63:0] ValE,
  output Cnd
);

  wire alu_1_negative, alu_1_overflow, alu_1_zero, and_1_out, and_2_out, comparator_1_eq, comparator_2_eq,
       or_1_out;
  wire [1:0] alufun_1_op;
  wire [7:0] counter_1_q;
  wire [63:0] alu_1_vale, alua_1_val1, alub_1_val2;

  and and_1 (and_1_out, clock, e);
  ALUA alua_1 (.valC(valC), .valA(valA), .icode(icode), .val1(alua_1_val1));
  ALUB alub_1 (.valB(valB), .icode(icode), .val2(alub_1_val2));
  ALUfun alufun_1 (.icode(icode), .ifun(ifun), .op(alufun_1_op));
  or or_1 (or_1_out, c, comparator_1_eq);
  Counter counter_1 (.clr(or_1_out), .count(1'b1), .clk(and_1_out), .Q(counter_1_q));  // open: load, up, D, carry
  ALU alu_1 (
    .val1(alua_1_val1), .val2(alub_1_val2), .op(alufun_1_op), .valE(alu_1_vale), .Negative(alu_1_negative),
    .Zero(alu_1_zero), .Overflow(alu_1_overflow));
  Comparator comparator_1 (.a(8'h14), .b(counter_1_q), .eq(comparator_1_eq));  // open: gt, lt
  Comparator comparator_2 (.a(8'hb), .b(counter_1_q), .eq(comparator_2_eq));  // open: gt, lt
  and and_2 (and_2_out, ~clock, comparator_2_eq);  // AND_Gate
  Register #(.width(64)) register_1 (.D(alu_1_vale), .en(1'b1), .clk(and_2_out), .Q(ValE));  // open: clr
  CC cc_1 (
    .icode(icode), .ifun(ifun), .overflow(alu_1_overflow), .zero(alu_1_zero), .negative(alu_1_negative),
    .clock(and_2_out), .cnd(Cnd));
endmodule

module CC (
  input  [3:0] icode,
  input  [3:0] ifun,
  input  overflow,
  input  zero,
  input  negative,
  input  clock,
  output cnd
);

  wire and_1_out, and_2_out, and_3_out, and_4_out, multiplexer_1_out, not_1_out, not_2_out, not_3_out,
       or_1_out, or_2_out, register_1_q, register_2_q, register_3_q, xor_1_out, xor_2_out, xor_3_out;

  and and_1 (and_1_out, ~icode[0], icode[1], icode[2], ~icode[3]);  // AND_Gate
  and and_2 (and_2_out, ~icode[0], icode[1], ~icode[2], ~icode[3]);  // AND_Gate
  and and_3 (and_3_out, icode[0], icode[1], icode[2], ~icode[3]);  // AND_Gate
  Register #(.width(1)) register_1 (.D(overflow), .en(and_1_out), .clk(clock), .Q(register_1_q));  // open: clr
  Register #(.width(1)) register_2 (.D(zero), .en(and_1_out), .clk(clock), .Q(register_2_q));  // open: clr
  Register #(.width(1)) register_3 (.D(negative), .en(and_1_out), .clk(clock), .Q(register_3_q));  // open: clr
  or or_1 (or_1_out, and_2_out, and_3_out);
  xor xor_1 (xor_1_out, register_3_q, register_1_q);
  xor xor_2 (xor_2_out, register_3_q, register_1_q);
  xor xor_3 (xor_3_out, register_1_q, register_3_q);
  not not_1 (not_1_out, register_2_q);
  or or_2 (or_2_out, xor_1_out, register_2_q);
  not not_2 (not_2_out, register_2_q);
  not not_3 (not_3_out, xor_3_out);
  and and_4 (and_4_out, not_3_out, not_1_out);
  Multiplexer #(.select(4)) multiplexer_1 (
    .in0(1'b1), .in1(or_2_out), .in2(xor_2_out), .in3(register_2_q), .in4(not_2_out), .in5(not_3_out),
    .in6(and_4_out), .out(multiplexer_1_out), .sel(ifun));  // open: in7, in8, in9, in10, in11, in12, in13, in14, in15
  Register #(.width(1)) register_4 (.D(multiplexer_1_out), .en(or_1_out), .clk(clock), .Q(cnd));  // open: clr

  // Notes on the sheet:
  //   OF
  //   ZF
  //   SF
endmodule

module decode (
  input  [63:0] WB_valM,
  input  [3:0] icode,
  input  [3:0] rA,
  input  [3:0] rB,
  input  c,
  input  e,
  input  clk,
  input  [63:0] WB_valE,
  output [63:0] valA,
  output [63:0] valB
);

  wire [3:0] decode1_1_dste, decode1_1_dstm, decode1_1_srca, decode1_1_srcb;

  decode1 decode1_1 (
    .iCode(icode), .rA(rA), .rB(rB), .srcA(decode1_1_srca), .srcB(decode1_1_srcb), .dstM(decode1_1_dstm),
    .dstE(decode1_1_dste));
  regFile regfile_1 (
    .W_dataM(WB_valM), .W_addrM(decode1_1_dstm), .R_addrA(decode1_1_srca), .WdataE(WB_valE),
    .W_addrE(decode1_1_dste), .R_addrB(decode1_1_srcb), .c(c), .e(e), .clk(clk), .valA(valA), .valB(valB));
endmodule

module decode1 (
  input  [3:0] iCode,
  input  [3:0] rA,
  input  [3:0] rB,
  output [3:0] srcA,
  output [3:0] srcB,
  output [3:0] dstM,
  output [3:0] dstE
);

  Multiplexer #(.select(4), .width(4)) multiplexer_1 (
    .in0(4'b1111), .in1(4'b1111), .in2(rA), .in3(4'b1111), .in4(rA), .in5(4'b1111), .in6(rA), .in7(4'b1111),
    .in8(4'b1111), .in9(4'b0100), .in10(rA), .in11(4'b0100), .in12(4'b1111), .in13(4'b1111), .in14(4'b1111),
    .in15(4'b1111), .out(srcA), .sel(iCode));
  Multiplexer #(.select(4), .width(4)) multiplexer_2 (
    .in0(4'b1111), .in1(4'b1111), .in2(4'b1111), .in3(4'b1111), .in4(rB), .in5(rB), .in6(rB), .in7(4'b1111),
    .in8(4'b0100), .in9(4'b0100), .in10(4'b0100), .in11(4'b0100), .in12(4'b1111), .in13(4'b1111),
    .in14(4'b1111), .in15(4'b1111), .out(srcB), .sel(iCode));
  Multiplexer #(.select(4), .width(4)) multiplexer_3 (
    .in0(4'b1111), .in1(4'b1111), .in2(4'b1111), .in3(4'b1111), .in4(4'b1111), .in5(rA), .in6(4'b1111),
    .in7(4'b1111), .in8(4'b1111), .in9(4'b1111), .in10(4'b1111), .in11(rA), .in12(4'b1111), .in13(4'b1111),
    .in14(4'b1111), .in15(4'b1111), .out(dstM), .sel(iCode));
  Multiplexer #(.select(4), .width(4)) multiplexer_4 (
    .in0(4'b1111), .in1(4'b1111), .in2(rB), .in3(rB), .in4(4'b1111), .in5(4'b1111), .in6(rB), .in7(4'b1111),
    .in8(4'b0100), .in9(4'b0100), .in10(4'b0100), .in11(4'b0100), .in12(4'b1111), .in13(4'b1111),
    .in14(4'b1111), .in15(4'b1111), .out(dstE), .sel(iCode));
endmodule

module memory (
  input  [3:0] iCode,
  input  [63:0] valA,
  input  [63:0] valE,
  input  [11:0] valP,
  input  e,
  input  c,
  input  clk,
  output [63:0] valM
);

  wire and_1_out, and_2_out, and_3_out, and_4_out, comparator_1_eq, comparator_2_eq, comparator_3_eq,
       comparator_4_eq, comparator_5_eq, comparator_6_eq, comparator_7_gt, comparator_8_lt, comparator_9_eq,
       decoder_1_out0, decoder_1_out1, decoder_1_out2, decoder_1_out3, decoder_1_out4, decoder_1_out5,
       decoder_1_out6, decoder_1_out7, memreadwrite_1_m_read, memreadwrite_1_m_write, or_1_out, undriven;
  wire [2:0] counter_1_q;
  wire [7:0] counter_2_q, memdatamemaddr_1_datain, memdatamemaddr_1_datain_2, memdatamemaddr_1_datain_3,
       memdatamemaddr_1_datain_4, memdatamemaddr_1_datain_5, memdatamemaddr_1_datain_6,
       memdatamemaddr_1_datain_7, memdatamemaddr_1_datain_8, multiplexer_1_out, multiplexer_2_out,
       multiplexer_3_out, multiplexer_4_out, multiplexer_5_out, multiplexer_6_out, multiplexer_7_out,
       multiplexer_8_out, multiplexer_9_out, ram_1_dout;
  wire [11:0] adder_1_out, bit_extender_1_out, memdatamemaddr_1_dataaddr;

  Multiplexer #(.select(3), .width(8)) multiplexer_1 (
    .in0(memdatamemaddr_1_datain_8), .in1(memdatamemaddr_1_datain_7), .in2(memdatamemaddr_1_datain_6),
    .in3(memdatamemaddr_1_datain_5), .in4(memdatamemaddr_1_datain_4), .in5(memdatamemaddr_1_datain_3),
    .in6(memdatamemaddr_1_datain_2), .in7(memdatamemaddr_1_datain), .out(multiplexer_1_out), .sel(counter_1_q));
  and and_1 (and_1_out, ~clk, and_4_out);  // AND_Gate
  MemReadWrite memreadwrite_1 (.iCode(iCode), .M_Read(memreadwrite_1_m_read), .M_Write(memreadwrite_1_m_write));
  MemDataMemAddr memdatamemaddr_1 (
    .iCode(iCode), .valA(valA), .valE(valE), .valP(valP),
    .dataIn({memdatamemaddr_1_datain_8, memdatamemaddr_1_datain_7, memdatamemaddr_1_datain_6, memdatamemaddr_1_datain_5, memdatamemaddr_1_datain_4, memdatamemaddr_1_datain_3, memdatamemaddr_1_datain_2, memdatamemaddr_1_datain}),
    .dataAddr(memdatamemaddr_1_dataaddr));
  Counter #(.max('h7), .width(3)) counter_1 (
    .clr(undriven), .up(1'b1), .count(e), .clk(and_1_out), .Q(counter_1_q));  // open: load, D, carry
  and and_2 (and_2_out, clk, and_4_out);
  and and_3 (and_3_out, clk, e);
  Adder #(.width(12)) adder_1 (
    .a(memdatamemaddr_1_dataaddr), .b(bit_extender_1_out), .out(adder_1_out));  // open: cin, cout
  assign bit_extender_1_out = {{9{1'b0}}, counter_1_q};  // Bit_Extender bit_extender_1
  Comparator #(.width(1)) comparator_1 (.a(1'b0), .b(and_2_out), .eq(comparator_1_eq));  // open: gt, lt
  Comparator #(.width(1)) comparator_2 (.a(1'b0), .b(comparator_1_eq), .eq(comparator_2_eq));  // open: gt, lt
  Counter counter_2 (.clr(or_1_out), .count(1'b1), .clk(and_3_out), .Q(counter_2_q));  // open: load, up, D, carry
  or or_1 (or_1_out, comparator_9_eq, c);
  RAM #(.addrWidth(12), .enables("line")) ram_1 (
    .addr(adder_1_out), .we(memreadwrite_1_m_write), .clk(and_1_out), .din(multiplexer_1_out),
    .dout(ram_1_dout));
  Comparator #(.width(1)) comparator_3 (.a(1'b0), .b(comparator_2_eq), .eq(comparator_3_eq));  // open: gt, lt
  Comparator #(.width(1)) comparator_4 (.a(1'b0), .b(comparator_3_eq), .eq(comparator_4_eq));  // open: gt, lt
  Comparator #(.width(1)) comparator_5 (.a(1'b0), .b(comparator_4_eq), .eq(comparator_5_eq));  // open: gt, lt
  Comparator #(.width(1)) comparator_6 (.a(1'b0), .b(comparator_5_eq), .eq(comparator_6_eq));  // open: gt, lt
  Decoder #(.select(3)) decoder_1 (
    .out0(decoder_1_out0), .out1(decoder_1_out1), .out2(decoder_1_out2), .out3(decoder_1_out3),
    .out4(decoder_1_out4), .out5(decoder_1_out5), .out6(decoder_1_out6), .out7(decoder_1_out7),
    .sel(counter_1_q));  // open: en
  Comparator comparator_7 (.a(counter_2_q), .b(8'hb), .gt(comparator_7_gt));  // open: eq, lt
  Comparator comparator_8 (.a(counter_2_q), .b(8'h14), .lt(comparator_8_lt));  // open: gt, eq
  Comparator comparator_9 (.a(8'h14), .b(counter_2_q), .eq(comparator_9_eq));  // open: gt, lt
  Multiplexer #(.width(8)) multiplexer_2 (
    .in0(valM[63:56]), .in1(ram_1_dout), .out(multiplexer_2_out), .sel(decoder_1_out0));
  Multiplexer #(.width(8)) multiplexer_3 (
    .in0(valM[55:48]), .in1(ram_1_dout), .out(multiplexer_3_out), .sel(decoder_1_out1));
  Multiplexer #(.width(8)) multiplexer_4 (
    .in0(valM[47:40]), .in1(ram_1_dout), .out(multiplexer_4_out), .sel(decoder_1_out2));
  Multiplexer #(.width(8)) multiplexer_5 (
    .in0(valM[39:32]), .in1(ram_1_dout), .out(multiplexer_5_out), .sel(decoder_1_out3));
  Multiplexer #(.width(8)) multiplexer_6 (
    .in0(valM[31:24]), .in1(ram_1_dout), .out(multiplexer_6_out), .sel(decoder_1_out4));
  Multiplexer #(.width(8)) multiplexer_7 (
    .in0(valM[23:16]), .in1(ram_1_dout), .out(multiplexer_7_out), .sel(decoder_1_out5));
  Multiplexer #(.width(8)) multiplexer_8 (
    .in0(valM[15:8]), .in1(ram_1_dout), .out(multiplexer_8_out), .sel(decoder_1_out6));
  Multiplexer #(.width(8)) multiplexer_9 (
    .in0(valM[7:0]), .in1(ram_1_dout), .out(multiplexer_9_out), .sel(decoder_1_out7));
  Register register_1 (
    .D(multiplexer_2_out), .en(memreadwrite_1_m_read), .clk(comparator_6_eq), .Q(valM[63:56]));  // open: clr
  Register register_2 (
    .D(multiplexer_3_out), .en(memreadwrite_1_m_read), .clk(comparator_6_eq), .Q(valM[55:48]));  // open: clr
  Register register_3 (
    .D(multiplexer_4_out), .en(memreadwrite_1_m_read), .clk(comparator_6_eq), .Q(valM[47:40]));  // open: clr
  Register register_4 (
    .D(multiplexer_5_out), .en(memreadwrite_1_m_read), .clk(comparator_6_eq), .Q(valM[39:32]));  // open: clr
  Register register_5 (
    .D(multiplexer_6_out), .en(memreadwrite_1_m_read), .clk(comparator_6_eq), .Q(valM[31:24]));  // open: clr
  Register register_6 (
    .D(multiplexer_7_out), .en(memreadwrite_1_m_read), .clk(comparator_6_eq), .Q(valM[23:16]));  // open: clr
  Register register_7 (
    .D(multiplexer_8_out), .en(memreadwrite_1_m_read), .clk(comparator_6_eq), .Q(valM[15:8]));  // open: clr
  Register register_8 (
    .D(multiplexer_9_out), .en(memreadwrite_1_m_read), .clk(comparator_6_eq), .Q(valM[7:0]));  // open: clr
  and and_4 (and_4_out, comparator_7_gt, comparator_8_lt);
endmodule

module MemDataMemAddr (
  input  [3:0] iCode,
  input  [63:0] valA,
  input  [63:0] valE,
  input  [11:0] valP,
  output [63:0] dataIn,
  output [11:0] dataAddr
);

  wire [7:0] multiplexer_2_out_2, multiplexer_2_out_3, multiplexer_2_out_4, multiplexer_2_out_5,
       multiplexer_2_out_6, multiplexer_2_out_7;
  wire [7:4] multiplexer_2_out;
  wire [63:0] bit_extender_1_out;

  assign bit_extender_1_out = {{52{valP[11]}}, valP};  // Bit_Extender bit_extender_1
  Multiplexer #(.select(4), .width(64)) multiplexer_1 (
    .in0(valA), .in1(valA), .in2(valA), .in3(valA), .in4(valA), .in5(valA), .in6(valA), .in7(valA),
    .in8(bit_extender_1_out), .in9(valA), .in10(valA), .in11(valA), .in12(valA), .in13(valA), .in14(valA),
    .in15(valA), .out(dataIn), .sel(iCode));
  Multiplexer #(.select(4), .width(64)) multiplexer_2 (
    .in0(valA), .in1(valA), .in2(valA), .in3(valA), .in4(valE), .in5(valE), .in6(valA), .in7(valA),
    .in8(valE), .in9(valA), .in10(valE), .in11(valA), .in12(valA), .in13(valA), .in14(valA), .in15(valA),
    .out({multiplexer_2_out_7, multiplexer_2_out_6, multiplexer_2_out_5, multiplexer_2_out_4, multiplexer_2_out_3, multiplexer_2_out_2, multiplexer_2_out, dataAddr}),
    .sel(iCode));
endmodule

module MemReadWrite (
  input  [3:0] iCode,
  output M_Read,
  output M_Write
);

  wire and_1_out, and_2_out, and_3_out, and_4_out, and_5_out, and_6_out;

  and and_1 (and_1_out, iCode[0], ~iCode[1], iCode[2], ~iCode[3]);  // AND_Gate
  and and_2 (and_2_out, iCode[0], iCode[1], ~iCode[2], iCode[3]);  // AND_Gate
  and and_3 (and_3_out, iCode[0], ~iCode[1], ~iCode[2], iCode[3]);  // AND_Gate
  and and_4 (and_4_out, ~iCode[0], ~iCode[1], ~iCode[2], iCode[3]);  // AND_Gate
  and and_5 (and_5_out, ~iCode[0], iCode[1], ~iCode[2], iCode[3]);  // AND_Gate
  and and_6 (and_6_out, ~iCode[0], ~iCode[1], iCode[2], ~iCode[3]);  // AND_Gate
  or or_1 (M_Read, and_1_out, and_2_out, and_3_out);
  or or_2 (M_Write, and_4_out, and_5_out, and_6_out);
endmodule

module pcUpdate (
  input  [3:0] iCode,
  input  [11:0] valP,
  input  [63:0] valC,
  input  [63:0] valM,
  input  Cnd,
  input  clk,
  input  c,
  input  e,
  output halt,
  output [11:0] PC
);

  wire and_1_out, and_2_out, and_4_out, comparator_1_lt, comparator_2_eq, comparator_3_eq, or_1_out;
  wire [7:0] counter_1_q;
  wire [11:0] multiplexer_1_out, multiplexer_2_out;

  Multiplexer #(.width(12)) multiplexer_1 (.in0(valP), .in1(valC[11:0]), .out(multiplexer_1_out), .sel(Cnd));
  Multiplexer #(.select(4), .width(12)) multiplexer_2 (
    .in0({12{1'b0}}), .in1(valP), .in2(valP), .in3(valP), .in4(valP), .in5(valP), .in6(valP),
    .in7(multiplexer_1_out), .in8(valC[11:0]), .in9({valM[15:12], valM[7:0]}), .in10(valP), .in11(valP),
    .out(multiplexer_2_out), .sel(iCode));  // open: in12, in13, in14, in15
  and and_1 (and_1_out, clk, e);
  and and_2 (and_2_out, ~iCode[0], ~iCode[1], ~iCode[2], ~iCode[3]);  // AND_Gate
  or or_1 (or_1_out, c, comparator_2_eq);
  Counter counter_1 (.clr(or_1_out), .count(1'b1), .clk(and_1_out), .Q(counter_1_q));  // open: load, up, D, carry
  Register #(.width(12)) register_1 (.D(multiplexer_2_out), .en(1'b1), .clk(and_4_out), .Q(PC));  // open: clr
  Comparator #(.width(12)) comparator_1 (.a({12{1'b0}}), .b(PC), .lt(comparator_1_lt));  // open: gt, eq
  Comparator comparator_2 (.a(8'h14), .b(counter_1_q), .eq(comparator_2_eq));  // open: gt, lt
  Comparator comparator_3 (.a({8{1'b0}}), .b(counter_1_q), .eq(comparator_3_eq));  // open: gt, lt
  and and_3 (halt, and_2_out, comparator_1_lt);
  and and_4 (and_4_out, ~clk, comparator_3_eq);  // AND_Gate
endmodule
