// Logisim project cpu.circ as structural Verilog
module instructionMem (
  input  [11:0] PC,
  input  clk,
  input  e,
  input  c,
  output [7:0] b0,
  output [7:0] b1,
  output [7:0] b2,
  output [7:0] b3,
  output [7:0] b4,
  output [7:0] b5,
  output [7:0] b6,
  output [7:0] b7,
  output [7:0] b8,
  output [7:0] b9
);

  wire and_5_out, decoder_1_out0, decoder_1_out1, decoder_1_out2, decoder_1_out3, decoder_1_out4,
       decoder_1_out5, decoder_1_out6, decoder_1_out7, decoder_1_out8, decoder_1_out9, or_1_out;
  wire [7:0] multiplexer_1_out, multiplexer_2_out, multiplexer_3_out, multiplexer_4_out, multiplexer_5_out,
       multiplexer_6_out, multiplexer_7_out, multiplexer_8_out, multiplexer_9_out, multiplexer_10_out,
       rom_1_data;
  wire [11:0] adder_1_out, counter_1_q;

  or or_1 (or_1_out, c, and_5_out);
  Counter #(.max('hfff), .width(12)) counter_1 (
    .clr(or_1_out), .up(1'b1), .clk(clk), .Q(counter_1_q));  // open: load, count, D, carry
  // AND_Gate and_1 is placed but not wired
  // AND_Gate and_2 is placed but not wired
  // AND_Gate and_3 is placed but not wired
  // AND_Gate and_4 is placed but not wired
  ROM #(.addrWidth(12)) rom_1 (.addr(adder_1_out), .data(rom_1_data));
  Adder #(.width(12)) adder_1 (.a(PC), .b(counter_1_q), .out(adder_1_out));  // open: cin, cout
  and and_5 (and_5_out, counter_1_q[3], ~counter_1_q[2], counter_1_q[1], ~counter_1_q[0]);  // AND_Gate
  Decoder #(.select(4)) decoder_1 (
    .out0(decoder_1_out0), .out1(decoder_1_out1), .out2(decoder_1_out2), .out3(decoder_1_out3),
    .out4(decoder_1_out4), .out5(decoder_1_out5), .out6(decoder_1_out6), .out7(decoder_1_out7),
    .out8(decoder_1_out8), .out9(decoder_1_out9), .sel(counter_1_q[3:0]));  // open: out10, out11, out12, out13, out14, out15, en
  Register register_1 (.D(multiplexer_1_out), .en(e), .clk(clk), .Q(b0));  // open: clr
  Multiplexer #(.width(8)) multiplexer_1 (.in0(b0), .in1(rom_1_data), .out(multiplexer_1_out), .sel(decoder_1_out0));
  Register register_2 (.D(multiplexer_2_out), .en(e), .clk(clk), .Q(b1));  // open: clr
  Multiplexer #(.width(8)) multiplexer_2 (.in0(b1), .in1(rom_1_data), .out(multiplexer_2_out), .sel(decoder_1_out1));
  Register register_3 (.D(multiplexer_3_out), .en(e), .clk(clk), .Q(b2));  // open: clr
  Multiplexer #(.width(8)) multiplexer_3 (.in0(b2), .in1(rom_1_data), .out(multiplexer_3_out), .sel(decoder_1_out2));
  Register register_4 (.D(multiplexer_4_out), .en(e), .clk(clk), .Q(b3));  // open: clr
  Multiplexer #(.width(8)) multiplexer_4 (.in0(b3), .in1(rom_1_data), .out(multiplexer_4_out), .sel(decoder_1_out3));
  Register register_5 (.D(multiplexer_5_out), .en(e), .clk(clk), .Q(b4));  // open: clr
  Multiplexer #(.width(8)) multiplexer_5 (.in0(b4), .in1(rom_1_data), .out(multiplexer_5_out), .sel(decoder_1_out4));
  Register register_6 (.D(multiplexer_6_out), .en(e), .clk(clk), .Q(b5));  // open: clr
  Multiplexer #(.width(8)) multiplexer_6 (.in0(b5), .in1(rom_1_data), .out(multiplexer_6_out), .sel(decoder_1_out5));
  Register register_7 (.D(multiplexer_7_out), .en(e), .clk(clk), .Q(b6));  // open: clr
  Multiplexer #(.width(8)) multiplexer_7 (.in0(b6), .in1(rom_1_data), .out(multiplexer_7_out), .sel(decoder_1_out6));
  Register register_8 (.D(multiplexer_8_out), .en(e), .clk(clk), .Q(b7));  // open: clr
  Multiplexer #(.width(8)) multiplexer_8 (.in0(b7), .in1(rom_1_data), .out(multiplexer_8_out), .sel(decoder_1_out7));
  Register register_9 (.D(multiplexer_9_out), .en(e), .clk(clk), .Q(b8));  // open: clr
  Multiplexer #(.width(8)) multiplexer_9 (.in0(b8), .in1(rom_1_data), .out(multiplexer_9_out), .sel(decoder_1_out8));
  Register register_10 (.D(multiplexer_10_out), .en(e), .clk(clk), .Q(b9));  // open: clr
  Multiplexer #(.width(8)) multiplexer_10 (.in0(b9), .in1(rom_1_data), .out(multiplexer_10_out), .sel(decoder_1_out9));

  // Notes on the sheet:
  //   contents of rom_1 (hex, n*v repeats v):
  //   20
endmodule

module fetch (
  input  [11:0] PC,
  input  clk,
  input  e,
  input  c,
  output [3:0] icode,
  output [3:0] ifun,
  output [3:0] rA,
  output [3:0] rB,
  output [63:0] valC,
  output [11:0] valP
);

  wire needsreg_1_needreg, needsvalc_1_needvalc;
  wire [7:0] instructionmem_1_b1, instructionmem_1_b2, instructionmem_1_b3, instructionmem_1_b4,
       instructionmem_1_b5, instructionmem_1_b6, instructionmem_1_b7, instructionmem_1_b8,
       instructionmem_1_b9;

  instructionMem instructionmem_1 (
    .PC(PC), .clk(clk), .e(e), .c(c), .b0({icode, ifun}), .b1(instructionmem_1_b1), .b2(instructionmem_1_b2),
    .b3(instructionmem_1_b3), .b4(instructionmem_1_b4), .b5(instructionmem_1_b5), .b6(instructionmem_1_b6),
    .b7(instructionmem_1_b7), .b8(instructionmem_1_b8), .b9(instructionmem_1_b9));
  needsReg needsreg_1 (.icode(icode), .needReg(needsreg_1_needreg));
  align align_1 (
    .needReg(needsreg_1_needreg), .b1(instructionmem_1_b1), .b2(instructionmem_1_b2),
    .b3(instructionmem_1_b3), .b4(instructionmem_1_b4), .b5(instructionmem_1_b5), .b6(instructionmem_1_b6),
    .b7(instructionmem_1_b7), .b8(instructionmem_1_b8), .b9(instructionmem_1_b9), .rA(rA), .rB(rB),
    .valC(valC));
  needsValC needsvalc_1 (.icode(icode), .needValC(needsvalc_1_needvalc));
  pcInc pcinc_1 (.PC(PC), .needsReg(needsreg_1_needreg), .needsValC(needsvalc_1_needvalc), .valP(valP));
endmodule

module align (
  input  needReg,
  input  [7:0] b1,
  input  [7:0] b2,
  input  [7:0] b3,
  input  [7:0] b4,
  input  [7:0] b5,
  input  [7:0] b6,
  input  [7:0] b7,
  input  [7:0] b8,
  input  [7:0] b9,
  output [3:0] rA,
  output [3:0] rB,
  output [63:0] valC
);

  Multiplexer #(.width(64)) multiplexer_1 (
    .in0({b1, b2, b3, b4, b5, b6, b7, b8}), .in1({b2, b3, b4, b5, b6, b7, b8, b9}), .out(valC), .sel(needReg));

  assign rA = b1[3:0];
  assign rB = b1[7:4];
endmodule

module needsReg (
  input  [3:0] icode,
  output needReg
);

  wire and_1_out, and_2_out, and_3_out, and_4_out, and_5_out, and_6_out, and_7_out;

  and and_1 (and_1_out, ~icode[0], icode[1], ~icode[2], ~icode[3]);  // AND_Gate
  and and_2 (and_2_out, icode[0], icode[1], ~icode[2], ~icode[3]);  // AND_Gate
  and and_3 (and_3_out, ~icode[0], ~icode[1], icode[2], ~icode[3]);  // AND_Gate
  and and_4 (and_4_out, icode[0], ~icode[1], icode[2], ~icode[3]);  // AND_Gate
  and and_5 (and_5_out, ~icode[0], icode[1], icode[2], ~icode[3]);  // AND_Gate
  and and_6 (and_6_out, ~icode[0], icode[1], ~icode[2], icode[3]);  // AND_Gate
  and and_7 (and_7_out, icode[0], icode[1], ~icode[2], icode[3]);  // AND_Gate
  or or_1 (needReg, and_1_out, and_2_out, and_3_out, and_4_out, and_5_out, and_6_out, and_7_out);
endmodule

module needsValC (
  input  [3:0] icode,
  output needValC
);

  wire and_1_out, and_2_out, and_3_out, and_4_out, and_5_out;

  and and_1 (and_1_out, icode[0], icode[1], ~icode[2], ~icode[3]);  // AND_Gate
  and and_2 (and_2_out, ~icode[0], ~icode[1], icode[2], ~icode[3]);  // AND_Gate
  and and_3 (and_3_out, icode[0], ~icode[1], icode[2], ~icode[3]);  // AND_Gate
  and and_4 (and_4_out, icode[0], icode[1], icode[2], ~icode[3]);  // AND_Gate
  and and_5 (and_5_out, ~icode[0], ~icode[1], ~icode[2], icode[3]);  // AND_Gate
  or or_1 (needValC, and_1_out, and_2_out, and_3_out, and_4_out, and_5_out);
endmodule

module pcInc (
  input  [11:0] PC,
  input  needsReg,
  input  needsValC,
  output [11:0] valP
);

  wire [11:0] adder_1_out, adder_2_out, multiplexer_1_out, multiplexer_2_out;

  Multiplexer #(.width(12)) multiplexer_1 (.in0({12{1'b0}}), .in1(12'h1), .out(multiplexer_1_out), .sel(needsReg));
  Multiplexer #(.width(12)) multiplexer_2 (.in0({12{1'b0}}), .in1(12'h8), .out(multiplexer_2_out), .sel(needsValC));
  Adder #(.width(12)) adder_1 (.a(multiplexer_1_out), .b(multiplexer_2_out), .out(adder_1_out));  // open: cin, cout
  Adder #(.width(12)) adder_2 (.a(12'h1), .b(adder_1_out), .out(adder_2_out));  // open: cin, cout
  Adder #(.width(12)) adder_3 (.a(PC), .b(adder_2_out), .out(valP));  // open: cin, cout
endmodule

module regFile (
  input  [63:0] W_dataM,
  input  clk,
  input  [3:0] W_addrM,
  input  [3:0] R_addrA,
  input  [63:0] W_dataE,
  input  [3:0] W_addrE,
  input  [3:0] R_addrB,
  output [63:0] valA,
  output [63:0] valB
);

  wire decoder_1_out0, decoder_1_out1, decoder_1_out2, decoder_1_out3, decoder_1_out4, decoder_1_out5,
       decoder_1_out6, decoder_1_out7, decoder_1_out8, decoder_1_out9, decoder_1_out10, decoder_1_out11,
       decoder_1_out12, decoder_1_out13, decoder_1_out14, decoder_1_out15, decoder_3_out0, decoder_3_out1,
       decoder_3_out2, decoder_3_out3, decoder_3_out4, decoder_3_out5, decoder_3_out6, decoder_3_out7,
       decoder_3_out8, decoder_3_out9, decoder_3_out10, decoder_3_out11, decoder_3_out12, decoder_3_out13,
       decoder_3_out14, decoder_3_out15, undriven, undriven_2, undriven_3, undriven_4, undriven_5,
       undriven_6, undriven_7, undriven_8, undriven_9, undriven_10, undriven_11, undriven_12, undriven_13,
       undriven_14, undriven_15, undriven_16;
  wire [63:0] bitselector_1_out, register_1_q, register_2_q, register_3_q, register_4_q, register_5_q,
       register_6_q, register_7_q, register_8_q, register_9_q, register_10_q, register_11_q, register_12_q,
       register_13_q, register_14_q, register_15_q, register_16_q;

  Decoder #(.select(4)) decoder_1 (
    .out0(decoder_1_out0), .out1(decoder_1_out1), .out2(decoder_1_out2), .out3(decoder_1_out3),
    .out4(decoder_1_out4), .out5(decoder_1_out5), .out6(decoder_1_out6), .out7(decoder_1_out7),
    .out8(decoder_1_out8), .out9(decoder_1_out9), .out10(decoder_1_out10), .out11(decoder_1_out11),
    .out12(decoder_1_out12), .out13(decoder_1_out13), .out14(decoder_1_out14), .out15(decoder_1_out15),
    .sel(W_addrM));  // open: en
  Decoder #(.select(4)) decoder_2 (.sel(W_addrE));  // open: out0, out1, out2, out3, out4, out5, out6, out7, out8, out9, out10, out11, out12, out13, out14, out15, en
  Register #(.width(64)) register_1 (.D(W_dataM), .en(decoder_1_out0), .clk(clk), .Q(register_1_q));  // open: clr
  Register #(.width(64)) register_2 (.D(W_dataM), .en(decoder_1_out1), .clk(clk), .Q(register_2_q));  // open: clr
  Register #(.width(64)) register_3 (.D(W_dataM), .en(decoder_1_out2), .clk(clk), .Q(register_3_q));  // open: clr
  Register #(.width(64)) register_4 (.D(W_dataM), .en(decoder_1_out3), .clk(clk), .Q(register_4_q));  // open: clr
  Register #(.width(64)) register_5 (.D(W_dataM), .en(decoder_1_out4), .clk(clk), .Q(register_5_q));  // open: clr
  Register #(.width(64)) register_6 (.D(W_dataM), .en(decoder_1_out5), .clk(clk), .Q(register_6_q));  // open: clr
  Register #(.width(64)) register_7 (.D(W_dataM), .en(decoder_1_out6), .clk(clk), .Q(register_7_q));  // open: clr
  Register #(.width(64)) register_8 (.D(W_dataM), .en(decoder_1_out7), .clk(clk), .Q(register_8_q));  // open: clr
  Register #(.width(64)) register_9 (.D(W_dataM), .en(decoder_1_out8), .clk(clk), .Q(register_9_q));  // open: clr
  Register #(.width(64)) register_10 (.D(W_dataM), .en(decoder_1_out9), .clk(clk), .Q(register_10_q));  // open: clr
  Register #(.width(64)) register_11 (.D(W_dataM), .en(decoder_1_out10), .clk(clk), .Q(register_11_q));  // open: clr
  Register #(.width(64)) register_12 (.D(W_dataM), .en(decoder_1_out11), .clk(clk), .Q(register_12_q));  // open: clr
  Register #(.width(64)) register_13 (.D(W_dataM), .en(decoder_1_out12), .clk(clk), .Q(register_13_q));  // open: clr
  Register #(.width(64)) register_14 (.D(W_dataM), .en(decoder_1_out13), .clk(clk), .Q(register_14_q));  // open: clr
  Register #(.width(64)) register_15 (.D(W_dataM), .en(decoder_1_out14), .clk(clk), .Q(register_15_q));  // open: clr
  Register #(.width(64)) register_16 (.D(W_dataM), .en(decoder_1_out15), .clk(clk), .Q(register_16_q));  // open: clr
  BitSelector #(.group(64), .width(64)) bitselector_1 (
    .in(register_1_q), .out(bitselector_1_out), .sel(decoder_3_out0));
  BitSelector #(.group(64), .width(64)) bitselector_2 (.in(register_1_q), .sel(undriven));  // open: out
  BitSelector #(.group(64), .width(64)) bitselector_3 (.in(register_2_q), .sel(decoder_3_out1));  // open: out
  BitSelector #(.group(64), .width(64)) bitselector_4 (.in(register_2_q), .sel(undriven_2));  // open: out
  BitSelector #(.group(64), .width(64)) bitselector_5 (.in(register_3_q), .sel(decoder_3_out2));  // open: out
  BitSelector #(.group(64), .width(64)) bitselector_6 (.in(register_3_q), .sel(undriven_3));  // open: out
  BitSelector #(.group(64), .width(64)) bitselector_7 (.in(register_4_q), .sel(decoder_3_out3));  // open: out
  BitSelector #(.group(64), .width(64)) bitselector_8 (.in(register_4_q), .sel(undriven_4));  // open: out
  BitSelector #(.group(64), .width(64)) bitselector_9 (.in(register_5_q), .sel(decoder_3_out4));  // open: out
  BitSelector #(.group(64), .width(64)) bitselector_10 (.in(register_5_q), .sel(undriven_5));  // open: out
  BitSelector #(.group(64), .width(64)) bitselector_11 (.in(register_6_q), .sel(decoder_3_out5));  // open: out
  BitSelector #(.group(64), .width(64)) bitselector_12 (.in(register_6_q), .sel(undriven_6));  // open: out
  BitSelector #(.group(64), .width(64)) bitselector_13 (.in(register_7_q), .sel(decoder_3_out6));  // open: out
  BitSelector #(.group(64), .width(64)) bitselector_14 (.in(register_7_q), .sel(undriven_7));  // open: out
  BitSelector #(.group(64), .width(64)) bitselector_15 (.in(register_8_q), .sel(decoder_3_out7));  // open: out
  BitSelector #(.group(64), .width(64)) bitselector_16 (.in(register_8_q), .sel(undriven_8));  // open: out
  BitSelector #(.group(64), .width(64)) bitselector_17 (.in(register_9_q), .sel(decoder_3_out8));  // open: out
  BitSelector #(.group(64), .width(64)) bitselector_18 (.in(register_9_q), .sel(undriven_9));  // open: out
  BitSelector #(.group(64), .width(64)) bitselector_19 (.in(register_10_q), .sel(decoder_3_out9));  // open: out
  BitSelector #(.group(64), .width(64)) bitselector_20 (.in(register_10_q), .sel(undriven_10));  // open: out
  BitSelector #(.group(64), .width(64)) bitselector_21 (.in(register_11_q), .sel(decoder_3_out10));  // open: out
  BitSelector #(.group(64), .width(64)) bitselector_22 (.in(register_11_q), .sel(undriven_11));  // open: out
  BitSelector #(.group(64), .width(64)) bitselector_23 (.in(register_12_q), .sel(decoder_3_out11));  // open: out
  BitSelector #(.group(64), .width(64)) bitselector_24 (.in(register_12_q), .sel(undriven_12));  // open: out
  BitSelector #(.group(64), .width(64)) bitselector_25 (.in(register_13_q), .sel(decoder_3_out12));  // open: out
  BitSelector #(.group(64), .width(64)) bitselector_26 (.in(register_13_q), .sel(undriven_13));  // open: out
  BitSelector #(.group(64), .width(64)) bitselector_27 (.in(register_14_q), .sel(decoder_3_out13));  // open: out
  BitSelector #(.group(64), .width(64)) bitselector_28 (.in(register_14_q), .sel(undriven_14));  // open: out
  BitSelector #(.group(64), .width(64)) bitselector_29 (.in(register_15_q), .sel(decoder_3_out14));  // open: out
  BitSelector #(.group(64), .width(64)) bitselector_30 (.in(register_15_q), .sel(undriven_15));  // open: out
  BitSelector #(.group(64), .width(64)) bitselector_31 (.in(register_16_q), .sel(decoder_3_out15));  // open: out
  BitSelector #(.group(64), .width(64)) bitselector_32 (.in(register_16_q), .sel(undriven_16));  // open: out
  Decoder #(.select(4)) decoder_3 (
    .out0(decoder_3_out0), .out1(decoder_3_out1), .out2(decoder_3_out2), .out3(decoder_3_out3),
    .out4(decoder_3_out4), .out5(decoder_3_out5), .out6(decoder_3_out6), .out7(decoder_3_out7),
    .out8(decoder_3_out8), .out9(decoder_3_out9), .out10(decoder_3_out10), .out11(decoder_3_out11),
    .out12(decoder_3_out12), .out13(decoder_3_out13), .out14(decoder_3_out14), .out15(decoder_3_out15),
    .sel(R_addrA));  // open: en
  Decoder #(.select(4)) decoder_4 (.sel(R_addrB));  // open: out0, out1, out2, out3, out4, out5, out6, out7, out8, out9, out10, out11, out12, out13, out14, out15, en
endmodule

module decode1 (
  input  [3:0] iCode,
  input  [3:0] rA,
  input  [3:0] rB,
  output [3:0] srcA,
  output [3:0] srcB,
  output [3:0] dstM,
  output [3:0] dstE
);

  Multiplexer #(.select(4), .width(4)) multiplexer_1 (
    .in0(4'b1111), .in1(4'b1111), .in2(rA), .in3(4'b1111), .in4(rA), .in5(4'b1111), .in6(rA), .in7(4'b1111),
    .in8(4'b1111), .in9(4'b0100), .in10(rA), .in11(4'b0100), .in12(4'b1111), .in13(4'b1111), .in14(4'b1111),
    .in15(4'b1111), .out(srcA), .sel(iCode));
  Multiplexer #(.select(4), .width(4)) multiplexer_2 (
    .in0(4'b1111), .in1(4'b1111), .in2(4'b1111), .in3(4'b1111), .in4(rB), .in5(rB), .in6(rB), .in7(4'b1111),
    .in8(4'b0100), .in9(4'b0100), .in10(4'b0100), .in11(4'b0100), .in12(4'b1111), .in13(4'b1111),
    .in14(4'b1111), .in15(4'b1111), .out(srcB), .sel(iCode));
  Multiplexer #(.select(4), .width(4)) multiplexer_3 (
    .in0(4'b1111), .in1(4'b1111), .in2(4'b1111), .in3(4'b1111), .in4(4'b1111), .in5(rA), .in6(4'b1111),
    .in7(4'b1111), .in8(4'b1111), .in9(4'b1111), .in10(4'b1111), .in11(rA), .in12(4'b1111), .in13(4'b1111),
    .in14(4'b1111), .in15(4'b1111), .out(dstM), .sel(iCode));
  Multiplexer #(.select(4), .width(4)) multiplexer_4 (
    .in0(4'b1111), .in1(4'b1111), .in2(4'b1111), .in3(4'b1111), .in4(4'b1111), .in5(4'b1111), .in6(rB),
    .in7(4'b1111), .in8(4'b0100), .in9(4'b0100), .in10(4'b0100), .in11(4'b0100), .in12(4'b1111),
    .in13(4'b1111), .in14(4'b1111), .in15(4'b1111), .out(dstE), .sel(iCode));
endmodule

module ALU (
  input  [63:0] val1,
  input  [63:0] val2,
  input  [1:0] op,
  output [63:0] valE,
  output Zero,
  output Overflow,
  output Negative
);

  wire [63:0] adder_1_out, and_1_out, subtractor_1_out, xor_1_out;

  Adder #(.width(64)) adder_1 (.a(val1), .b(val2), .out(adder_1_out));  // open: cin, cout
  Subtractor #(.width(64)) subtractor_1 (.a(val2), .b(val1), .out(subtractor_1_out));  // open: bin, bout
  assign and_1_out = val2 & val1;  // AND_Gate and_1, 64 bits wide
  assign xor_1_out = val1 ^ val2;  // XOR_Gate xor_1, 64 bits wide
  Multiplexer #(.select(2), .width(64)) multiplexer_1 (
    .in0(adder_1_out), .in1(subtractor_1_out), .in2(and_1_out), .in3(xor_1_out), .out(valE), .sel(op));
endmodule

module ALUB (
  input  [63:0] valB,
  input  [3:0] icode,
  output [63:0] val2
);

  wire and_1_out, and_2_out, or_1_out;

  and and_1 (and_1_out, ~icode[0], icode[1], ~icode[2], ~icode[3]);  // AND_Gate
  or or_1 (or_1_out, and_1_out, and_2_out);
  Multiplexer #(.width(64)) multiplexer_1 (.in0(valB), .in1({64{1'b0}}), .out(val2), .sel(or_1_out));
  and and_2 (and_2_out, icode[0], icode[1], ~icode[2], ~icode[3]);  // AND_Gate
endmodule

module ALUA (
  input  [63:0] valC,
  input  [63:0] valA,
  input  [3:0] icode,
  output [63:0] val1
);

  wire and_1_out, and_2_out, and_3_out, and_4_out, and_5_out;
  wire [1:0] or_1_out;

  and and_1 (and_1_out, ~icode[0], ~icode[1], icode[2], ~icode[3]);  // AND_Gate
  or or_1 (or_1_out[0], and_1_out, and_3_out, and_2_out);
  and and_2 (and_2_out, icode[0], ~icode[1], icode[2], ~icode[3]);  // AND_Gate
  and and_3 (and_3_out, icode[0], icode[1], ~icode[2], ~icode[3]);  // AND_Gate
  Multiplexer #(.select(2), .width(64)) multiplexer_1 (
    .in0(64'h8), .in1(valC), .in2(valA), .out(val1), .sel(or_1_out));  // open: in3
  or or_2 (or_1_out[1], and_4_out, and_5_out);
  and and_4 (and_4_out, ~icode[0], icode[1], ~icode[2], ~icode[3]);  // AND_Gate
  and and_5 (and_5_out, ~icode[0], icode[1], icode[2], ~icode[3]);  // AND_Gate
endmodule

module ALUfun (
  input  [3:0] icode,
  input  [3:0] ifun,
  output [1:0] op
);

  wire and_1_out, and_2_out, and_3_out, and_4_out, and_5_out, nor_1_out, or_1_out;

  nor nor_1 (nor_1_out, or_1_out, and_5_out, and_4_out);
  and and_1 (and_1_out, ~icode[0], icode[1], icode[2], ~icode[3], ifun[0], ~ifun[1], ~ifun[2], ~ifun[3]);  // AND_Gate
  or or_1 (or_1_out, and_1_out, and_2_out, and_3_out);
  and and_2 (and_2_out, ~icode[0], ~icode[1], ~icode[2], icode[3]);  // AND_Gate
  and and_3 (and_3_out, ~icode[0], icode[1], ~icode[2], icode[3]);  // AND_Gate
  Priority_Encoder #(.select(2)) priority_encoder_1 (
    .in0(nor_1_out), .in1(or_1_out), .in2(and_4_out), .in3(and_5_out), .out(op));
  and and_4 (and_4_out, ~icode[0], icode[1], icode[2], ~icode[3], ~ifun[0], ifun[1], ~ifun[2], ~ifun[3]);  // AND_Gate
  and and_5 (and_5_out, ~icode[0], icode[1], icode[2], ~icode[3], ifun[0], ifun[1], ~ifun[2], ~ifun[3]);  // AND_Gate
endmodule

module execute (
  input  [3:0] icode,
  input  [3:0] ifun,
  input  [63:0] valA,
  input  [63:0] valB,
  input  [63:0] valC,
  output [63:0] ValE,
  output Cnd
);

  wire alu_1_negative, alu_1_overflow, alu_1_zero;
  wire [1:0] alufun_1_op;
  wire [63:0] alua_1_val1, alub_1_val2;

  ALUA alua_1 (.valC(valC), .valA(valA), .icode(icode), .val1(alua_1_val1));
  ALUB alub_1 (.valB(valB), .icode(icode), .val2(alub_1_val2));
  ALUfun alufun_1 (.icode(icode), .ifun(ifun), .op(alufun_1_op));
  ALU alu_1 (
    .val1(alua_1_val1), .val2(alub_1_val2), .op(alufun_1_op), .valE(ValE), .Zero(alu_1_zero),
    .Overflow(alu_1_overflow), .Negative(alu_1_negative));
  CC cc_1 (
    .icode(icode), .ifun(ifun), .overflow(alu_1_overflow), .zero(alu_1_zero), .negative(alu_1_negative),
    .cnd(Cnd));
endmodule

module CC (
  input  [3:0] icode,
  input  [3:0] ifun,
  input  overflow,
  input  zero,
  input  negative,
  output cnd
);
endmodule
